// Logisim project Sagui_Vetorial.circ as structural Verilog: 5 circuits, main circuit main
module main (
);

  wire Br, clock_1_out, IsBr, MD, RAD, spe_ula_1_zero, W, WE;
  wire [1:0] multiplexer_2_out, USr;
  wire [2:0] UOp;
  wire [3:0] Opcode, rom_1_data;
  wire [7:0] adder_1_out, bit_extender_1_out, Data, multiplexer_1_out, multiplexer_3_out,
       program_counter_1_pc_n, RA, ram_1_dout, RB, spe_ula_1_out_4;

  Multiplexer #(.width(8)) multiplexer_1 (.in0(adder_1_out), .in1(RB), .out(multiplexer_1_out), .sel(IsBr));
  Clock clock_1 (.out(clock_1_out));
  Program_Counter program_counter_1 (
    .PC_P(multiplexer_1_out), .Clk(clock_1_out), .PC_N(program_counter_1_pc_n));  // open: R
  Adder adder_1 (.a(program_counter_1_pc_n), .b(8'h1), .out(adder_1_out));  // open: cin, cout
  ROM rom_1 (.addr(program_counter_1_pc_n), .data({Opcode, rom_1_data}));
  Multiplexer #(.width(2)) multiplexer_2 (.in0(rom_1_data[3:2]), .in1(2'b01), .out(multiplexer_2_out), .sel(RAD));
  assign bit_extender_1_out = {{4{rom_1_data[3]}}, rom_1_data};  // Bit_Extender bit_extender_1
  Control_Unit control_unit_1 (
    .Opcode(Opcode), .WE(WE), .RadSpe(RAD), .UlaOpSpe(UOp), .UlaSrSpe(USr), .BrSpe(Br), .MD(MD), .WM(W));  // open: Vec
  SPE_Register_Bank spe_register_bank_1 (
    .WE(WE), .Data(Data), .RD(multiplexer_2_out), .Clk(clock_1_out), .RA(multiplexer_2_out),
    .RB(rom_1_data[1:0]), .RD1(RA), .RD2(RB));  // open: R
  Multiplexer #(.select(2), .width(8)) multiplexer_3 (
    .in0(RB), .in1(bit_extender_1_out), .in2({8{1'b0}}), .in3({8{1'b0}}), .out(multiplexer_3_out), .sel(USr));
  SPE_ULA spe_ula_1 (.ULA_Op(UOp), .RA(RA), .RB(multiplexer_3_out), .out_4(spe_ula_1_out_4), .Zero(spe_ula_1_zero));
  and and_1 (IsBr, Br, spe_ula_1_zero);
  RAM ram_1 (.addr(RB), .we(W), .oe(1'b1), .clk(clock_1_out), .din(RA), .dout(ram_1_dout));
  Multiplexer #(.width(8)) multiplexer_4 (.in0(spe_ula_1_out_4), .in1(ram_1_dout), .out(Data), .sel(MD));

  // Notes on the sheet:
  //   contents of rom_1 (hex, n*v repeats v):
  //   2c 39
endmodule

module SPE_Register_Bank (
  input  [7:0] Data,
  input  [1:0] RA,
  input  WE,
  input  [1:0] RD,
  input  [1:0] RB,
  input  Clk,
  input  R,
  output [7:0] RD1,
  output [7:0] RD2
);

  wire demultiplexer_1_out0, R1, R2, R3;
  wire [7:0] D1, D2, D3;

  // NoConnect on demultiplexer_1_out0
  Demultiplexer #(.select(2)) demultiplexer_1 (
    .out0(demultiplexer_1_out0), .out1(R1), .out2(R2), .out3(R3), .in(WE), .sel(RD));
  Register u_R1 (.D(Data), .en(R1), .clk(Clk), .Q(D1), .clr(R));
  Register u_R2 (.D(Data), .en(R2), .clk(Clk), .Q(D2), .clr(R));
  Register u_R3 (.D(Data), .en(R3), .clk(Clk), .Q(D3), .clr(R));
  Multiplexer #(.select(2), .width(8)) multiplexer_1 (
    .in0({8{1'b0}}), .in1(D1), .in2(D2), .in3(D3), .out(RD1), .sel(RA));
  Multiplexer #(.select(2), .width(8)) multiplexer_2 (
    .in0({8{1'b0}}), .in1(D1), .in2(D2), .in3(D3), .out(RD2), .sel(RB));

  // Notes on the sheet:
  //   R0
endmodule

module SPE_ULA (
  input  [7:0] RA,
  input  [7:0] RB,
  input  [2:0] ULA_Op,
  output [7:0] out_4,
  output Zero
);

  wire [7:0] R2, R3, R4;

  // NoConnect on RA[7:4]
  // NoConnect on RB[7:4]
  // NoConnect on RB[7:4]
  // NoConnect on RA[3:0]
  Adder adder_1 (.a(RA), .b(RB), .out(R2));  // open: cin, cout
  Subtractor subtractor_1 (.a(RA), .b(RB), .out(R3));  // open: bin, bout
  assign R4 = RA & RB;  // AND_Gate and_1, 8 bits wide
  Multiplexer #(.select(3), .width(8)) multiplexer_1 (
    .in0({RB[3:0], RA[3:0]}), .in1({RA[7:4], RB[3:0]}), .in2(R2), .in3(R3), .in4(R4), .in5({8{1'b0}}),
    .in6({8{1'b0}}), .in7({8{1'b0}}), .out(out_4), .sel(ULA_Op));
  nor nor_1 (Zero, R3[0], R3[1], R3[2], R3[3], R3[4], R3[5], R3[6], R3[7]);

  // Other names for the same wires on the sheet: R0[7:0] = {RB[3:0], RA[3:0]}; R1[7:0] = {RA[7:4], RB[3:0]}

  // Notes on the sheet:
  //   Move High
  //   Move Low
  //   Adder
  //   Subtractor
  //   AND
endmodule

module Program_Counter (
  input  [7:0] PC_P,
  input  Clk,
  input  R,
  output [7:0] PC_N
);

  Register register_1 (.D(PC_P), .en(1'b1), .clk(Clk), .Q(PC_N), .clr(R));
endmodule

module Control_Unit (
  input  [3:0] Opcode,
  output Vec,
  output WE,
  output RadSpe,
  output [2:0] UlaOpSpe,
  output [1:0] UlaSrSpe,
  output BrSpe,
  output MD,
  output WM
);

  ROM #(.addrWidth(4), .dataWidth(11)) rom_1 (
    .addr(Opcode), .data({Vec, WE, RadSpe, UlaOpSpe, UlaSrSpe, BrSpe, MD, WM}));

  // Notes on the sheet:
  //   contents of rom_1 (hex, n*v repeats v):
  //   202 1 308 328 240 260 280 14 8*400
endmodule
