// Logisim project t2v0.circ as structural Verilog: 4 circuits, main circuit main
module main (
);

  wire and_1_out, branchOK, brzrOK, clk, JIJR, or_1_out, reset_out, SelBranch, ULAsrc, WBR, WDU, WMD;
  wire [3:0] imm4, ULAop;
  wire [7:0] A, adder_1_out, adder_2_out, B, branch, imm8, memdata, multiplexer_1_out, multiplexer_2_out,
       multiplexer_4_out, saidaPC, ULAdata;
  wire [7:4] inst;

  and and_1 (and_1_out, brzrOK, branchOK);
  Adder adder_1 (.a(branch), .b(saidaPC), .out(adder_1_out));  // open: cin, cout
  Adder adder_2 (.a(8'h1), .b(saidaPC), .out(adder_2_out));  // open: cin, cout
  or or_1 (or_1_out, JIJR, and_1_out);
  Multiplexer #(.width(8)) multiplexer_1 (
    .in0(adder_2_out), .in1(adder_1_out), .out(multiplexer_1_out), .sel(or_1_out));
  Register PC (.D(multiplexer_1_out), .en(1'b1), .clk(clk), .Q(saidaPC), .clr(reset_out));
  Button reset (.out(reset_out));
  Multiplexer #(.width(8)) multiplexer_2 (.in0(ULAdata), .in1(memdata), .out(multiplexer_2_out), .sel(WDU));
  Clock #(.highDuration(2), .lowDuration(2)) clock_1 (.out(clk));
  dual_port_ram dual_port_ram_1 (.addr(B), .pc(saidaPC), .d(ULAdata), .w(WMD), .instr({inst, imm4}), .data(memdata));
  BancoReg bancoreg_1 (
    .clk(clk), .d(multiplexer_2_out), .w(WBR), .SelW(imm4[3:2]), .SelA(imm4[3:2]), .SelB(imm4[1:0]), .A(A),
    .B(B));
  extSinal extsinal_1 (.imm4(imm4), .imm8(imm8));
  Multiplexer #(.width(8)) multiplexer_3 (.in0(B), .in1(imm8), .out(branch), .sel(SelBranch));
  Multiplexer #(.width(8)) multiplexer_4 (.in0(B), .in1(imm8), .out(multiplexer_4_out), .sel(ULAsrc));
  ROM #(.addrWidth(4), .dataWidth(11)) rom_1 (
    .addr(inst), .data({WDU, WBR, WMD, ULAsrc, ULAop, SelBranch, branchOK, JIJR}));
  ULA ula_1 (.A(A), .B(multiplexer_4_out), .Seletor(ULAop), .brzr(brzrOK), .R(ULAdata));

  // Other names for the same wires on the sheet: inst[3:0] = imm4; rb[1:0] = imm4[1:0]; ra[1:0] = imm4[3:2]

  // Notes on the sheet:
  //   Mux para selecionar ra ou r0? Para addi e multi
  //   Mem de Inst e Dados
  //   contents of rom_1 (hex, n*v repeats v):
  //   1a a5 624 124 2a0 2b8 234 21 204 20c 214 21c 224 22c 244 24c
  //   Mem de Controle
endmodule

module ULA (
  input  [7:0] A,
  input  [7:0] B,
  input  [3:0] Seletor,
  output brzr,
  output [7:0] R
);

  wire [7:0] R0, R1, R2, R3, R4, R5, R6, R7, R8, R9;

  Multiplexer #(.select(4), .width(8)) multiplexer_1 (
    .in0(R0), .in1(R1), .in2(R2), .in3(R3), .in4(R4), .in5(R5), .in6(R6), .in7(R7), .in8(R8), .in9(R9),
    .out(R), .sel(Seletor));  // open: in10, in11, in12, in13, in14, in15
  assign R0 = ~B;  // NOT_Gate not_1, 8 bits wide
  assign R1 = A & B;  // AND_Gate and_1, 8 bits wide
  assign R2 = A | B;  // OR_Gate or_1, 8 bits wide
  assign R3 = A ^ B;  // XOR_Gate xor_1, 8 bits wide
  Adder adder_1 (.a(A), .b(B), .out(R4));  // open: cin, cout
  Subtractor subtractor_1 (.a(A), .b(B), .out(R5));  // open: bin, bout
  Subtractor subtractor_2 (.a(A), .b(8'h1), .out(R6));  // open: bin, bout
  Multiplier multiplier_1 (.a(A), .b(B), .out(R7));  // open: cin, cout
  Shifter shifter_1 (.in(A), .\dist (B[2:0]), .out(R8));
  Shifter #(.shift("lr")) shifter_2 (.in(A), .\dist (B[2:0]), .out(R9));
  Comparator comparator_1 (.a(A), .b({8{1'b0}}), .eq(brzr));  // open: gt, lt

  // Notes on the sheet:
  //   Add
  //   Sub
  //   Dec
  //   Mult
  //   Slr
  //   Srr
endmodule

module BancoReg (
  input  clk,
  input  [7:0] d,
  input  w,
  input  [1:0] SelW,
  input  [1:0] SelA,
  input  [1:0] SelB,
  output [7:0] A,
  output [7:0] B
);

  wire undriven, undriven_2, undriven_3, undriven_4, w0, w1, w2, w3;
  wire [7:0] l0, l1, l2, l3;

  Demultiplexer #(.select(2)) demultiplexer_1 (.out0(w0), .out1(w1), .out2(w2), .out3(w3), .in(w), .sel(SelW));
  Multiplexer #(.select(2), .width(8)) multiplexer_1 (.in0(l0), .in1(l1), .in2(l2), .in3(l3), .out(A), .sel(SelA));
  Multiplexer #(.select(2), .width(8)) multiplexer_2 (.in0(l0), .in1(l1), .in2(l2), .in3(l3), .out(B), .sel(SelB));
  Register r0 (.D(d), .en(w0), .clk(clk), .Q(l0), .clr(undriven));
  // NoConnect on undriven
  Register r1 (.D(d), .en(w1), .clk(clk), .Q(l1), .clr(undriven_2));
  // NoConnect on undriven_2
  Register r2 (.D(d), .en(w2), .clk(clk), .Q(l2), .clr(undriven_3));
  Register r3 (.D(d), .en(w3), .clk(clk), .Q(l3), .clr(undriven_4));
  // NoConnect on undriven_3
  // NoConnect on undriven_4

  // Other names for the same wires on the sheet: data[7:0] = d

  // Notes on the sheet:
  //   Escrita
  //   Leitura A
  //   Leitura B
endmodule

module extSinal (
  input  [3:0] imm4,
  output [7:0] imm8
);


  assign imm8 = {{5{imm4[3]}}, imm4[2:0]};
endmodule
