// Logisim project Sagui_Vetorial.circ as structural Verilog: 17 circuits, main circuit main
module main (
);

  wire Br, Clk, IsBr, MD, MD0, MD1, MD2, MD3, Nop, R, RAD, RAD0, RAD1, RAD2, RAD3, spe_ula_1_zero, USr0,
       USr1, USr2, USr3, W, WE, WE0, WE1, WE2, WE3, WM0, WM1, WM2, WM3;
  wire [1:0] ID, IdV0, IdV1, IdV2, IdV3, MEM, MemV0, MemV1, MemV2, MemV3, multiplexer_2_out,
       multiplexer_3_out, multiplexer_4_out, multiplexer_5_out, multiplexer_6_out, RA_ID, RB_ID, USr;
  wire [2:0] UOp, UOp0, UOp1, UOp2, UOp3;
  wire [3:0] ExeV0, ExeV1, ExeV2, ExeV3, Opcode;
  wire [5:0] EXE;
  wire [7:0] adder_1_out, d0, d1, d2, d3, Data, imm, multiplexer_1_out, multiplexer_8_out, multiplexer_9_out,
       multiplexer_10_out, multiplexer_11_out, multiplexer_13_out, program_counter_1_pc_n, RA, RA0, RA1, RA2,
       RA3, RB, RB0, RB1, RB2, RB3, spe_memory_data_1_data, spe_ula_1_out_4, vpe_memory_data_1_data,
       vpe_memory_data_2_data, vpe_memory_data_3_data, vpe_memory_data_4_data, vpe_ula_1_out_4,
       vpe_ula_2_out_4, vpe_ula_3_out_4, vpe_ula_4_out_4, VS;

  Multiplexer #(.width(8)) multiplexer_1 (.in0(adder_1_out), .in1(RB), .out(multiplexer_1_out), .sel(IsBr));
  Program_Counter program_counter_1 (.PC_P(multiplexer_1_out), .Clk(Clk), .R(R), .PC_N(program_counter_1_pc_n));
  Adder adder_1 (.a(program_counter_1_pc_n), .b(8'h1), .out(adder_1_out));  // open: cin, cout
  Clock clock_1 (.out(Clk));
  Button Reset (.out(R));
  Memory_Instruction memory_instruction_1 (.Addr_PC(program_counter_1_pc_n), .Inst({Opcode, RA_ID, RB_ID}));
  VPE_Ctrl vpe_ctrl_1 (.VectorSigns(VS), .ID_V(IdV0), .EXE_V(ExeV0), .MEM_V(MemV0));
  VPE_Ctrl vpe_ctrl_2 (.VectorSigns(VS), .ID_V(IdV1), .EXE_V(ExeV1), .MEM_V(MemV1));
  VPE_Ctrl vpe_ctrl_3 (.VectorSigns(VS), .ID_V(IdV2), .EXE_V(ExeV2), .MEM_V(MemV2));
  VPE_Ctrl vpe_ctrl_4 (.VectorSigns(VS), .ID_V(IdV3), .EXE_V(ExeV3), .MEM_V(MemV3));
  Multiplexer #(.width(2)) multiplexer_2 (.in0(RA_ID), .in1(2'b01), .out(multiplexer_2_out), .sel(RAD));
  Multiplexer #(.width(2)) multiplexer_3 (.in0(RA_ID), .in1(2'b01), .out(multiplexer_3_out), .sel(RAD0));
  Multiplexer #(.width(2)) multiplexer_4 (.in0(RA_ID), .in1(2'b01), .out(multiplexer_4_out), .sel(RAD1));
  Multiplexer #(.width(2)) multiplexer_5 (.in0(RA_ID), .in1(2'b01), .out(multiplexer_5_out), .sel(RAD2));
  Multiplexer #(.width(2)) multiplexer_6 (.in0(RA_ID), .in1(2'b01), .out(multiplexer_6_out), .sel(RAD3));
  Multiplexer #(.width(2)) multiplexer_7 (.in0(ID), .in1(2'b00), .out({RAD, WE}), .sel(Nop));
  assign imm = {{4{RA_ID[1]}}, {RA_ID, RB_ID}};  // Bit_Extender bit_extender_1
  SPE_Register_Bank spe_register_bank_1 (
    .WE(WE), .Data(Data), .RD(multiplexer_2_out), .Clk(Clk), .R(R), .RA(multiplexer_2_out), .RB(RB_ID),
    .RD1(RA), .RD2(RB));
  Control_Unit control_unit_1 (
    .Opcode(Opcode), .Vec(Nop), .WE(ID[0]), .RadSpe(ID[1]), .UlaOpSpe(EXE[2:0]), .UlaSrSpe(EXE[4:3]),
    .BrSpe(EXE[5]), .MD(MEM[0]), .WM(MEM[1]), .VecSg(VS));
  VPE_RegBCtrSgs vpe_regbctrsgs_1 (.IdV(IdV0), .nop(Nop), .RAD0(RAD0), .WE0(WE0));
  VPE0_Register_Bank vpe0_register_bank_1 (
    .WE(WE0), .Data(d0), .RD(multiplexer_3_out), .Clk(Clk), .R(R), .RA(multiplexer_3_out), .RB(RB_ID),
    .RD1(RA0), .RD2(RB0));
  VPE_RegBCtrSgs vpe_regbctrsgs_2 (.IdV(IdV1), .nop(Nop), .RAD0(RAD1), .WE0(WE1));
  VPE_RegBCtrSgs vpe_regbctrsgs_3 (.IdV(IdV2), .nop(Nop), .RAD0(RAD2), .WE0(WE2));
  VPE_RegBCtrSgs vpe_regbctrsgs_4 (.IdV(IdV3), .nop(Nop), .RAD0(RAD3), .WE0(WE3));
  VPE1_Register_Bank vpe1_register_bank_1 (
    .WE(WE1), .Data(d1), .RD(multiplexer_4_out), .Clk(Clk), .R(R), .RA(multiplexer_4_out), .RB(RB_ID),
    .RD1(RA1), .RD2(RB1));
  VPE2_Register_Bank vpe2_register_bank_1 (
    .WE(WE2), .Data(d2), .RD(multiplexer_5_out), .Clk(Clk), .R(R), .RA(multiplexer_5_out), .RB(RB_ID),
    .RD1(RA2), .RD2(RB2));
  VPE3_Register_Bank vpe3_register_bank_1 (
    .WE(WE3), .Data(d3), .RD(multiplexer_6_out), .Clk(Clk), .R(R), .RA(multiplexer_6_out), .RB(RB_ID),
    .RD1(RA3), .RD2(RB3));
  Multiplexer #(.select(2), .width(8)) multiplexer_8 (
    .in0(RB), .in1(imm), .in2({8{1'b0}}), .in3({8{1'b0}}), .out(multiplexer_8_out), .sel(USr));
  Multiplexer #(.width(8)) multiplexer_9 (.in0(RB1), .in1(imm), .out(multiplexer_9_out), .sel(USr1));
  Multiplexer #(.width(8)) multiplexer_10 (.in0(RB2), .in1(imm), .out(multiplexer_10_out), .sel(USr2));
  Multiplexer #(.width(8)) multiplexer_11 (.in0(RB3), .in1(imm), .out(multiplexer_11_out), .sel(USr3));
  Multiplexer #(.width(6)) multiplexer_12 (.in0(EXE), .in1({6{1'b0}}), .out({Br, USr, UOp}), .sel(Nop));
  Multiplexer #(.width(8)) multiplexer_13 (.in0(RB0), .in1(imm), .out(multiplexer_13_out), .sel(USr0));
  SPE_ULA spe_ula_1 (.ULA_Op(UOp), .RA(RA), .RB(multiplexer_8_out), .out_4(spe_ula_1_out_4), .Zero(spe_ula_1_zero));
  VPE_ALUCtrSgs vpe_aluctrsgs_1 (.ExeV(ExeV0), .nop(Nop), .UOp(UOp0), .USr(USr0));
  VPE_ULA vpe_ula_1 (.ULA_Op(UOp0), .RA(RA0), .RB(multiplexer_13_out), .out_4(vpe_ula_1_out_4));
  VPE_ALUCtrSgs vpe_aluctrsgs_2 (.ExeV(ExeV1), .nop(Nop), .UOp(UOp1), .USr(USr1));
  VPE_ULA vpe_ula_2 (.ULA_Op(UOp1), .RA(RA1), .RB(multiplexer_9_out), .out_4(vpe_ula_2_out_4));
  VPE_ALUCtrSgs vpe_aluctrsgs_3 (.ExeV(ExeV2), .nop(Nop), .UOp(UOp2), .USr(USr2));
  VPE_ULA vpe_ula_3 (.ULA_Op(UOp2), .RA(RA2), .RB(multiplexer_10_out), .out_4(vpe_ula_3_out_4));
  VPE_ALUCtrSgs vpe_aluctrsgs_4 (.ExeV(ExeV3), .nop(Nop), .UOp(UOp3), .USr(USr3));
  VPE_ULA vpe_ula_4 (.ULA_Op(UOp3), .RA(RA3), .RB(multiplexer_11_out), .out_4(vpe_ula_4_out_4));
  and and_1 (IsBr, Br, spe_ula_1_zero);
  VPE_MemCtrSgs vpe_memctrsgs_1 (.MemV(MemV0), .nop(Nop), .MD(MD0), .WM(WM0));
  VPE_Memory_Data vpe_memory_data_1 (.Addr(RB0), .WM(WM0), .Clk(Clk), .d(RA0), .data(vpe_memory_data_1_data));
  VPE_MemCtrSgs vpe_memctrsgs_2 (.MemV(MemV1), .nop(Nop), .MD(MD1), .WM(WM1));
  VPE_Memory_Data vpe_memory_data_2 (.Addr(RB1), .WM(WM1), .Clk(Clk), .d(RA1), .data(vpe_memory_data_2_data));
  VPE_MemCtrSgs vpe_memctrsgs_3 (.MemV(MemV2), .nop(Nop), .MD(MD2), .WM(WM2));
  VPE_Memory_Data vpe_memory_data_3 (.Addr(RB2), .WM(WM2), .Clk(Clk), .d(RA2), .data(vpe_memory_data_3_data));
  VPE_MemCtrSgs vpe_memctrsgs_4 (.MemV(MemV3), .nop(Nop), .MD(MD3), .WM(WM3));
  VPE_Memory_Data vpe_memory_data_4 (.Addr(RB3), .WM(WM3), .Clk(Clk), .d(RA3), .data(vpe_memory_data_4_data));
  Multiplexer #(.width(2)) multiplexer_14 (.in0(MEM), .in1(2'b00), .out({W, MD}), .sel(Nop));
  SPE_Memory_Data spe_memory_data_1 (.Addr(RB), .WM(W), .Clk(Clk), .d(RA), .data(spe_memory_data_1_data));
  Multiplexer #(.width(8)) multiplexer_15 (.in0(vpe_ula_1_out_4), .in1(vpe_memory_data_1_data), .out(d0), .sel(MD0));
  Multiplexer #(.width(8)) multiplexer_16 (.in0(vpe_ula_2_out_4), .in1(vpe_memory_data_2_data), .out(d1), .sel(MD1));
  Multiplexer #(.width(8)) multiplexer_17 (.in0(vpe_ula_3_out_4), .in1(vpe_memory_data_3_data), .out(d2), .sel(MD2));
  Multiplexer #(.width(8)) multiplexer_18 (.in0(vpe_ula_4_out_4), .in1(vpe_memory_data_4_data), .out(d3), .sel(MD3));
  Multiplexer #(.width(8)) multiplexer_19 (.in0(spe_ula_1_out_4), .in1(spe_memory_data_1_data), .out(Data), .sel(MD));

  // Notes on the sheet:
  //   VPE0: control signs
  //   VPE1: control signs
  //   VPE2: control signs
  //   VPE3: control signs
  //   Register bank's control signs
  //   VPE0: Register bank's control signs
  //   VPE1: Register bank's control signs
  //   VPE2: Register bank's control signs
  //   VPE3: Register bank's control signs
  //   ALU's control signs
  //   =============================== Vector Processing Element ===============================
  //   VPE0: ALU's control signs
  //   VPE1: ALU's control signs
  //   VPE2: ALU's control signs
  //   VPE3: ALU's control signs
  //   =============================== Scalar Processing Element ===============================
  //   VPE0: Memory's control signs
  //   VPE1: Memory's control signs
  //   VPE2: Memory's control signs
  //   VPE3: Memory's control signs
  //   Register bank's control signs
endmodule

module Program_Counter (
  input  [7:0] PC_P,
  input  Clk,
  input  R,
  output [7:0] PC_N
);

  Register register_1 (.D(PC_P), .en(1'b1), .clk(Clk), .Q(PC_N), .clr(R));
endmodule

module Memory_Instruction (
  input  [7:0] Addr_PC,
  output [7:0] Inst
);

  ROM rom_1 (.addr(Addr_PC), .data(Inst));

  // Notes on the sheet:
  //   contents of rom_1 (hex, n*v repeats v):
  //   c8 b0 99 b4 c9 b1 99 b4 c9 b2 99 bc c9 b3 99 b4 c9 b4 99 c9 b5 c9
endmodule

module Control_Unit (
  input  [3:0] Opcode,
  output Vec,
  output WE,
  output RadSpe,
  output [2:0] UlaOpSpe,
  output [1:0] UlaSrSpe,
  output BrSpe,
  output MD,
  output WM,
  output [7:0] VecSg
);

  ROM #(.addrWidth(4), .dataWidth(19)) rom_1 (
    .addr(Opcode), .data({Vec, WE, RadSpe, UlaOpSpe, UlaSrSpe, BrSpe, MD, WM, VecSg}));

  // Notes on the sheet:
  //   contents of rom_1 (hex, n*v repeats v):
  //   20200 100 30800 32800 24000 26000 28000 1400 40082 40001 400c4 400cc 40090 40098 400a0 400a8
  //   Total de bits: 19
  //   0..7: signs of the vector part
  //   8..18: signs of the scalar part
  //   19: control bit between scalar and vector instructions
endmodule

module SPE_Register_Bank (
  input  [7:0] Data,
  input  [1:0] RA,
  input  WE,
  input  [1:0] RD,
  input  [1:0] RB,
  input  Clk,
  input  R,
  output [7:0] RD1,
  output [7:0] RD2
);

  wire demultiplexer_1_out0, R1, R2, R3;
  wire [7:0] D1, D2, D3;

  // NoConnect on demultiplexer_1_out0
  Demultiplexer #(.select(2)) demultiplexer_1 (
    .out0(demultiplexer_1_out0), .out1(R1), .out2(R2), .out3(R3), .in(WE), .sel(RD));
  Register SR1 (.D(Data), .en(R1), .clk(Clk), .Q(D1), .clr(R));
  Register SR2 (.D(Data), .en(R2), .clk(Clk), .Q(D2), .clr(R));
  Register SR3 (.D(Data), .en(R3), .clk(Clk), .Q(D3), .clr(R));
  Multiplexer #(.select(2), .width(8)) multiplexer_1 (
    .in0({8{1'b0}}), .in1(D1), .in2(D2), .in3(D3), .out(RD1), .sel(RA));
  Multiplexer #(.select(2), .width(8)) multiplexer_2 (
    .in0({8{1'b0}}), .in1(D1), .in2(D2), .in3(D3), .out(RD2), .sel(RB));

  // Notes on the sheet:
  //   SR0
endmodule

module SPE_ULA (
  input  [7:0] RA,
  input  [7:0] RB,
  input  [2:0] ULA_Op,
  output [7:0] out_4,
  output Zero
);

  wire [7:0] R2, R3, R4;

  // NoConnect on RA[7:4]
  // NoConnect on RB[7:4]
  // NoConnect on RB[7:4]
  // NoConnect on RA[3:0]
  Adder adder_1 (.a(RA), .b(RB), .out(R2));  // open: cin, cout
  Subtractor subtractor_1 (.a(RA), .b(RB), .out(R3));  // open: bin, bout
  assign R4 = RA & RB;  // AND_Gate and_1, 8 bits wide
  Multiplexer #(.select(3), .width(8)) multiplexer_1 (
    .in0({RB[3:0], RA[3:0]}), .in1({RA[7:4], RB[3:0]}), .in2(R2), .in3(R3), .in4(R4), .in5({8{1'b0}}),
    .in6({8{1'b0}}), .in7({8{1'b0}}), .out(out_4), .sel(ULA_Op));
  nor nor_1 (Zero, R3[0], R3[1], R3[2], R3[3], R3[4], R3[5], R3[6], R3[7]);

  // Other names for the same wires on the sheet: R0[7:0] = {RB[3:0], RA[3:0]}; R1[7:0] = {RA[7:4], RB[3:0]}

  // Notes on the sheet:
  //   Move High
  //   Move Low
  //   Adder
  //   Subtractor
  //   AND
endmodule

module SPE_Memory_Data (
  input  [7:0] Addr,
  input  WM,
  input  Clk,
  input  [7:0] d,
  output [7:0] data
);

  RAM ram_1 (.addr(Addr), .we(WM), .oe(1'b1), .clk(Clk), .din(d), .dout(data));
endmodule

module VPE_Ctrl (
  input  [7:0] VectorSigns,
  output [1:0] ID_V,
  output [3:0] EXE_V,
  output [1:0] MEM_V
);


  assign EXE_V = {VectorSigns[2], VectorSigns[5:3]};
  assign ID_V = VectorSigns[7:6];
  assign MEM_V = VectorSigns[1:0];
endmodule

module VPE_RegBCtrSgs (
  input  [1:0] IdV,
  input  nop,
  output RAD0,
  output WE0
);

  Multiplexer #(.width(2)) multiplexer_1 (.in0(2'b00), .in1(IdV), .out({WE0, RAD0}), .sel(nop));
endmodule

module VPE_ALUCtrSgs (
  input  [3:0] ExeV,
  input  nop,
  output [2:0] UOp,
  output USr
);

  Multiplexer #(.width(4)) multiplexer_1 (.in0(4'b0000), .in1(ExeV), .out({USr, UOp}), .sel(nop));
endmodule

module VPE_MemCtrSgs (
  input  [1:0] MemV,
  input  nop,
  output MD,
  output WM
);

  Multiplexer #(.width(2)) multiplexer_1 (.in0(2'b00), .in1(MemV), .out({MD, WM}), .sel(nop));
endmodule

module VPE0_Register_Bank (
  input  [7:0] Data,
  input  [1:0] RA,
  input  WE,
  input  [1:0] RD,
  input  [1:0] RB,
  input  Clk,
  input  R,
  output [7:0] RD1,
  output [7:0] RD2
);

  wire demultiplexer_1_out0, R1, R2, R3;
  wire [7:0] D1, D2, D3;

  // NoConnect on demultiplexer_1_out0
  Demultiplexer #(.select(2)) demultiplexer_1 (
    .out0(demultiplexer_1_out0), .out1(R1), .out2(R2), .out3(R3), .in(WE), .sel(RD));
  Register VR1 (.D(Data), .en(R1), .clk(Clk), .Q(D1), .clr(R));
  Register VR2 (.D(Data), .en(R2), .clk(Clk), .Q(D2), .clr(R));
  Register VR3 (.D(Data), .en(R3), .clk(Clk), .Q(D3), .clr(R));
  Multiplexer #(.select(2), .width(8)) multiplexer_1 (
    .in0({8{1'b0}}), .in1(D1), .in2(D2), .in3(D3), .out(RD1), .sel(RA));
  Multiplexer #(.select(2), .width(8)) multiplexer_2 (
    .in0({8{1'b0}}), .in1(D1), .in2(D2), .in3(D3), .out(RD2), .sel(RB));

  // Notes on the sheet:
  //   VR0
endmodule

module VPE1_Register_Bank (
  input  [7:0] Data,
  input  [1:0] RA,
  input  WE,
  input  [1:0] RD,
  input  [1:0] RB,
  input  Clk,
  input  R,
  output [7:0] RD1,
  output [7:0] RD2
);

  wire demultiplexer_1_out0, R1, R2, R3;
  wire [7:0] D1, D2, D3;

  // NoConnect on demultiplexer_1_out0
  Demultiplexer #(.select(2)) demultiplexer_1 (
    .out0(demultiplexer_1_out0), .out1(R1), .out2(R2), .out3(R3), .in(WE), .sel(RD));
  Register VR1 (.D(Data), .en(R1), .clk(Clk), .Q(D1), .clr(R));
  Register VR2 (.D(Data), .en(R2), .clk(Clk), .Q(D2), .clr(R));
  Register VR3 (.D(Data), .en(R3), .clk(Clk), .Q(D3), .clr(R));
  Multiplexer #(.select(2), .width(8)) multiplexer_1 (.in0(8'h1), .in1(D1), .in2(D2), .in3(D3), .out(RD1), .sel(RA));
  Multiplexer #(.select(2), .width(8)) multiplexer_2 (.in0(8'h1), .in1(D1), .in2(D2), .in3(D3), .out(RD2), .sel(RB));

  // Notes on the sheet:
  //   VR0
endmodule

module VPE2_Register_Bank (
  input  [7:0] Data,
  input  [1:0] RA,
  input  WE,
  input  [1:0] RD,
  input  [1:0] RB,
  input  Clk,
  input  R,
  output [7:0] RD1,
  output [7:0] RD2
);

  wire demultiplexer_1_out0, R1, R2, R3;
  wire [7:0] D1, D2, D3;

  // NoConnect on demultiplexer_1_out0
  Demultiplexer #(.select(2)) demultiplexer_1 (
    .out0(demultiplexer_1_out0), .out1(R1), .out2(R2), .out3(R3), .in(WE), .sel(RD));
  Register VR1 (.D(Data), .en(R1), .clk(Clk), .Q(D1), .clr(R));
  Register VR2 (.D(Data), .en(R2), .clk(Clk), .Q(D2), .clr(R));
  Register VR3 (.D(Data), .en(R3), .clk(Clk), .Q(D3), .clr(R));
  Multiplexer #(.select(2), .width(8)) multiplexer_1 (.in0(8'h2), .in1(D1), .in2(D2), .in3(D3), .out(RD1), .sel(RA));
  Multiplexer #(.select(2), .width(8)) multiplexer_2 (.in0(8'h2), .in1(D1), .in2(D2), .in3(D3), .out(RD2), .sel(RB));

  // Notes on the sheet:
  //   VR0
endmodule

module VPE3_Register_Bank (
  input  [7:0] Data,
  input  [1:0] RA,
  input  WE,
  input  [1:0] RD,
  input  [1:0] RB,
  input  Clk,
  input  R,
  output [7:0] RD1,
  output [7:0] RD2
);

  wire demultiplexer_1_out0, R1, R2, R3;
  wire [7:0] D1, D2, D3;

  // NoConnect on demultiplexer_1_out0
  Demultiplexer #(.select(2)) demultiplexer_1 (
    .out0(demultiplexer_1_out0), .out1(R1), .out2(R2), .out3(R3), .in(WE), .sel(RD));
  Register VR1 (.D(Data), .en(R1), .clk(Clk), .Q(D1), .clr(R));
  Register VR2 (.D(Data), .en(R2), .clk(Clk), .Q(D2), .clr(R));
  Register VR3 (.D(Data), .en(R3), .clk(Clk), .Q(D3), .clr(R));
  Multiplexer #(.select(2), .width(8)) multiplexer_1 (.in0(8'h3), .in1(D1), .in2(D2), .in3(D3), .out(RD1), .sel(RA));
  Multiplexer #(.select(2), .width(8)) multiplexer_2 (.in0(8'h3), .in1(D1), .in2(D2), .in3(D3), .out(RD2), .sel(RB));

  // Notes on the sheet:
  //   VR0
endmodule

module VPE_ULA (
  input  [7:0] RA,
  input  [7:0] RB,
  input  [2:0] ULA_Op,
  output [7:0] out_4
);

  wire comparator_1_eq;
  wire [7:0] R2, R3, R4, R5;

  // NoConnect on RA[7:4]
  // NoConnect on RB[7:4]
  // NoConnect on RB[7:4]
  // NoConnect on RA[3:0]
  Adder adder_1 (.a(RA), .b(RB), .out(R2));  // open: cin, cout
  Subtractor subtractor_1 (.a(RA), .b(RB), .out(R3));  // open: bin, bout
  assign R4 = RA & RB;  // AND_Gate and_1, 8 bits wide
  assign R5 = {{7{comparator_1_eq}}, comparator_1_eq};  // Bit_Extender bit_extender_1
  Comparator comparator_1 (.a(RA), .b(RB), .eq(comparator_1_eq));  // open: gt, lt
  Multiplexer #(.select(3), .width(8)) multiplexer_1 (
    .in0({RB[3:0], RA[3:0]}), .in1({RA[7:4], RB[3:0]}), .in2(R2), .in3(R3), .in4(R4), .in5(R5), .out(out_4),
    .sel(ULA_Op));  // open: in6, in7

  // Other names for the same wires on the sheet: R0[7:0] = {RB[3:0], RA[3:0]}; R1[7:0] = {RA[7:4], RB[3:0]}

  // Notes on the sheet:
  //   Move High
  //   Move Low
  //   Adder
  //   Subtractor
endmodule

module VPE_Memory_Data (
  input  [7:0] Addr,
  input  WM,
  input  Clk,
  input  [7:0] d,
  output [7:0] data
);

  RAM #(.trigger("falling")) ram_1 (.addr(Addr), .we(WM), .oe(1'b1), .clk(Clk), .din(d), .dout(data));
endmodule
