// Logisim project Sagui_VetorialP.circ as structural Verilog: 24 circuits, main circuit main
module main (
);

  wire Br, Clk, comparator_1_eq, En, hnop, IsBr, MD, multiplexer_20_out, or_1_out, or_2_out, R, V_Id, V_MD,
       V_MRd, V_MSti, V_RAD, V_USr, V_WE, V_WM, Vec, W, WB, WE, WS_Ex, WS_Me;
  wire [0:0] ID;
  wire [1:0] FA, FB, FBr, MEM, Mem_ID, MS_Ex, multiplexer_4_out, multiplexer_5_out, multiplexer_7_out,
       multiplexer_8_out, multiplexer_10_out, multiplexer_11_out, multiplexer_19_p3, RA, RA_EX, RA_ID, RB_EX,
       RB_ID, RD_EX, RD_ME, RD_WB, USr, V_Mem, VRA_ID, VRD_ID;
  wire [2:0] UOp, V_UOp, V_WB, WB_ID;
  wire [3:0] EXE_ID, Opcode, V_Exe;
  wire [4:0] EXE, multiplexer_18_p3;
  wire [7:0] adder_1_out, Addr, AE, AE3, d, d0, d1, d2, d3, DE, DE3, imm, imm_ex, memory_instruction_1_inst,
       multiplexer_1_out, multiplexer_2_out, multiplexer_6_out, multiplexer_9_out, multiplexer_12_out,
       multiplexer_15_out, multiplexer_16_out, multiplexer_21_out, multiplexer_22_out, multiplexer_23_out,
       multiplexer_27_out, multiplexer_29_out, multiplexer_35_out, N_Ptr0, N_Ptr1, N_Ptr2, N_Ptr3,
       program_counter_1_pc_n, RA0, RA1, RA2, RB0, RB1, RB2, RB3, RiUla, RUla, RWB, spe_memory_data_1_data,
       spe_register_bank_1_rd1, spe_register_bank_1_rd2, stg_id_ex_spe_1_rd1_exe, stg_id_ex_spe_1_rd2_exe,
       vpe3_register_bank_1_rd1, vpe3_register_bank_1_rd2, vpe_memory_data_1_data, vpe_memory_data_2_data,
       vpe_memory_data_3_data, vpe_memory_data_4_data, vpe_ula_1_out_4, vpe_ula_2_out_4, vpe_ula_3_out_4,
       vpe_ula_4_out_4;
  wire [9:0] VS;

  Multiplexer #(.width(8)) multiplexer_1 (.in0(adder_1_out), .in1(AE), .out(multiplexer_1_out), .sel(IsBr));
  Program_Counter program_counter_1 (
    .PC_P(multiplexer_1_out), .En(En), .Clk(Clk), .R(R), .PC_N(program_counter_1_pc_n));
  Clock clock_1 (.out(Clk));
  Button Reset (.out(R));
  Adder adder_1 (.a(program_counter_1_pc_n), .b(8'h1), .out(adder_1_out));  // open: cin, cout
  Memory_Instruction memory_instruction_1 (.Addr_PC(program_counter_1_pc_n), .Inst(memory_instruction_1_inst));
  Multiplexer #(.width(8)) multiplexer_2 (
    .in0(memory_instruction_1_inst), .in1(8'h40), .out(multiplexer_2_out), .sel(or_1_out));
  or or_1 (or_1_out, hnop, R);
  Stg_IF_ID stg_if_id_1 (.Inst_IF(multiplexer_2_out), .En(En), .Clk(Clk), .R(R), .Inst_ID({Opcode, RA, RB_ID}));
  // NoConnect on MS_Ex[1]
  Multiplexer #(.width(2)) multiplexer_3 (.in0(RA), .in1(2'b01), .out(RA_ID), .sel(ID[0]));
  VPE_Ctrl vpe_ctrl_1 (.VectorSigns(VS), .ID_V(V_Id), .EXE_V(V_Exe), .MEM_V(V_Mem), .WB_V(V_WB));
  Hazard_Unit hazard_unit_1 (
    .RD_ex(RD_EX), .RB_id(RA_ID), .RA_id(RA_ID), .MemRead(MS_Ex[0]), .Br(Br), .hnop(hnop), .EN(En));
  assign imm = {{4{RA_ID[1]}}, {RA_ID, RB_ID}};  // Bit_Extender bit_extender_1
  Multiplexer #(.width(2)) multiplexer_4 (.in0(RA), .in1(2'b01), .out(multiplexer_4_out), .sel(V_RAD));
  Multiplexer #(.width(2)) multiplexer_5 (.in0(multiplexer_4_out), .in1(RB_ID), .out(multiplexer_5_out), .sel(V_MRd));
  Multiplexer #(.width(8)) multiplexer_6 (.in0(d0), .in1(N_Ptr0), .out(multiplexer_6_out), .sel(V_MSti));
  Multiplexer #(.width(2)) multiplexer_7 (.in0(RA), .in1(2'b01), .out(multiplexer_7_out), .sel(V_RAD));
  Multiplexer #(.width(2)) multiplexer_8 (.in0(multiplexer_7_out), .in1(RB_ID), .out(multiplexer_8_out), .sel(V_MRd));
  Multiplexer #(.width(8)) multiplexer_9 (.in0(d1), .in1(N_Ptr1), .out(multiplexer_9_out), .sel(V_MSti));
  Multiplexer #(.width(2)) multiplexer_10 (.in0(RA), .in1(2'b01), .out(multiplexer_10_out), .sel(V_RAD));
  Multiplexer #(.width(2)) multiplexer_11 (
    .in0(multiplexer_10_out), .in1(RB_ID), .out(multiplexer_11_out), .sel(V_MRd));
  Multiplexer #(.width(8)) multiplexer_12 (.in0(d2), .in1(N_Ptr2), .out(multiplexer_12_out), .sel(V_MSti));
  Multiplexer #(.width(2)) multiplexer_13 (.in0(RA), .in1(2'b01), .out(VRA_ID), .sel(V_RAD));
  Multiplexer #(.width(2)) multiplexer_14 (.in0(VRA_ID), .in1(RB_ID), .out(VRD_ID), .sel(V_MRd));
  Multiplexer #(.width(8)) multiplexer_15 (.in0(d3), .in1(N_Ptr3), .out(multiplexer_15_out), .sel(V_MSti));
  SPE_Register_Bank spe_register_bank_1 (
    .WE(WE), .Data(RWB), .RD(RD_WB), .Clk(Clk), .R(R), .RA(RA_ID), .RB(RB_ID), .RD1(spe_register_bank_1_rd1),
    .RD2(spe_register_bank_1_rd2));
  Control_Unit control_unit_1 (
    .Opcode(Opcode), .Vec(Vec), .WESpe(WB), .RadSpe(ID[0]), .UlaOpSpe(EXE[2:0]), .UlaSrSpe(EXE[4:3]),
    .BrSpe(Br), .MDSpe(MEM[0]), .WMSpe(MEM[1]), .VecSg(VS));
  Multiplexer #(.select(2), .width(8)) multiplexer_16 (
    .in0(spe_register_bank_1_rd1), .in1(RUla), .in2(RiUla), .in3({8{1'b0}}), .out(multiplexer_16_out),
    .sel(FBr));
  Multiplexer multiplexer_17 (.in0(1'b0), .in1(V_Id), .out(V_RAD), .sel(Vec));
  Comparator comparator_1 (.a(multiplexer_16_out), .b({8{1'b0}}), .eq(comparator_1_eq));  // open: gt, lt
  ForwardingBranch_Unit forwardingbranch_unit_1 (
    .Rd_ExMem(RD_ME), .Rd_IdEx(RD_EX), .Ra_id(RA_ID), .WE_IdEx(WS_Ex), .WE_ExMem(WS_Me), .Forw_Br(FBr));
  VPE0_Register_Bank vpe0_register_bank_1 (
    .WE(V_WE), .Data(multiplexer_6_out), .RD(multiplexer_5_out), .Clk(Clk), .R(R), .RA(multiplexer_4_out),
    .RB(RB_ID), .RD1(RA0), .RD2(RB0));
  VPE1_Register_Bank vpe1_register_bank_1 (
    .WE(V_WE), .Data(multiplexer_9_out), .RD(multiplexer_8_out), .Clk(Clk), .R(R), .RA(multiplexer_7_out),
    .RB(RB_ID), .RD1(RA1), .RD2(RB1));
  VPE2_Register_Bank vpe2_register_bank_1 (
    .WE(V_WE), .Data(multiplexer_12_out), .RD(multiplexer_11_out), .Clk(Clk), .R(R), .RA(multiplexer_10_out),
    .RB(RB_ID), .RD1(RA2), .RD2(RB2));
  VPE3_Register_Bank vpe3_register_bank_1 (
    .WE(V_WE), .Data(multiplexer_15_out), .RD(VRD_ID), .Clk(Clk), .R(R), .RA(VRA_ID), .RB(RB_ID),
    .RD1(vpe3_register_bank_1_rd1), .RD2(vpe3_register_bank_1_rd2));
  or or_2 (or_2_out, Vec, hnop);
  // Multiplexer #(.width(5)) multiplexer_18: pin names not known; wires that end beside it: EXE, {5{1'b0}}, multiplexer_18_p3
  // Multiplexer #(.width(2)) multiplexer_19: pin names not known; wires that end beside it: MEM, 2'b00, multiplexer_19_p3
  Multiplexer multiplexer_20 (.in0(WB), .in1(1'b0), .out(multiplexer_20_out), .sel(or_2_out));
  and and_1 (IsBr, Br, comparator_1_eq);
  Multiplexer #(.width(8)) multiplexer_21 (.in0(RB0), .in1(imm), .out(multiplexer_21_out), .sel(V_USr));
  Multiplexer #(.width(8)) multiplexer_22 (.in0(RB1), .in1(imm), .out(multiplexer_22_out), .sel(V_USr));
  Multiplexer #(.width(8)) multiplexer_23 (.in0(RB2), .in1(imm), .out(multiplexer_23_out), .sel(V_USr));
  Stg_ID_EX_Spe stg_id_ex_spe_1 (
    .Imm_Id(imm), .ExeSgn_Id(multiplexer_18_p3), .MemSgn_Id(multiplexer_19_p3),
    .WbSgn_Id(multiplexer_20_out), .RD1_Id(spe_register_bank_1_rd1), .RD2_Id(spe_register_bank_1_rd2),
    .ARs_Id({RA_ID, RB_ID, RA_ID}), .Clk(Clk), .R(R), .Imm_Exe(imm_ex), .ExeSgn_Exe({USr, UOp}),
    .MemSgn_Exe(MS_Ex), .WbSgn_Exe(WS_Ex), .RD1_Exe(stg_id_ex_spe_1_rd1_exe),
    .RD2_Exe(stg_id_ex_spe_1_rd2_exe), .ARs_Exe({RD_EX, RB_EX, RA_EX}));
  Multiplexer #(.width(4)) multiplexer_24 (.in0(4'b0000), .in1(V_Exe), .out(EXE_ID), .sel(Vec));
  VPE_ULA vpe_ula_1 (.ULA_Op(V_UOp), .RA(RA0), .RB(multiplexer_21_out), .out_4(vpe_ula_1_out_4));
  VPE_ULA vpe_ula_2 (.ULA_Op(V_UOp), .RA(RA1), .RB(multiplexer_22_out), .out_4(vpe_ula_2_out_4));
  VPE_ULA vpe_ula_3 (.ULA_Op(V_UOp), .RA(RA2), .RB(multiplexer_23_out), .out_4(vpe_ula_3_out_4));
  Stg_ID_EX_Vpe stg_id_ex_vpe_1 (
    .Imm_Id(imm), .ExeSgn_Id(EXE_ID), .MemSgn_Id(Mem_ID), .WbSgn_Id(WB_ID),
    .RD1_Id(vpe3_register_bank_1_rd1), .RD2_Id(vpe3_register_bank_1_rd2), .ARs_Id({VRD_ID, RB_ID, VRA_ID}),
    .Clk(Clk), .R(R));  // open: Imm_Exe, ExeSgn_Exe, MemSgn_Exe, WbSgn_Exe, RD1_Exe, RD2_Exe, ARs_Exe
  Multiplexer #(.select(2), .width(8)) multiplexer_25 (
    .in0(stg_id_ex_spe_1_rd1_exe), .in1(RWB), .in2(RUla), .in3({8{1'b0}}), .out(DE), .sel(FA));
  Multiplexer #(.select(2), .width(8)) multiplexer_26 (
    .in0(stg_id_ex_spe_1_rd2_exe), .in1(RWB), .in2(RUla), .in3({8{1'b0}}), .out(AE));  // open: sel
  Multiplexer #(.select(2), .width(8)) multiplexer_27 (
    .in0(AE), .in1(imm_ex), .in2({8{1'b0}}), .in3({8{1'b0}}), .out(multiplexer_27_out), .sel(USr));
  Multiplexer #(.width(2)) multiplexer_28 (.in0(2'b00), .in1(V_Mem), .out(Mem_ID), .sel(Vec));
  Adder adder_2 (.a(8'h4), .b(RB0), .out(N_Ptr0));  // open: cin, cout
  Adder adder_3 (.a(8'h4), .b(RB1), .out(N_Ptr1));  // open: cin, cout
  Adder adder_4 (.a(8'h4), .b(RB2), .out(N_Ptr2));  // open: cin, cout
  Multiplexer #(.width(8)) multiplexer_29 (.in0(AE3), .out(multiplexer_29_out), .sel(V_USr));  // open: in1
  ForwardingULA_Unit forwardingula_unit_1 (
    .Rd_MemWb(RD_WB), .Rd_ExMem(RD_ME), .Rb(RB_EX), .Ra(RA_EX), .WE_ExMem(WS_Me), .WE_MemWb(WE), .Forw_A(FA),
    .Forw_B(FB));
  VPE_Memory_Data vpe_memory_data_1 (.Addr(RB0), .WM(V_WM), .Clk(Clk), .d(RA0), .data(vpe_memory_data_1_data));
  VPE_Memory_Data vpe_memory_data_2 (.Addr(RB1), .WM(V_WM), .Clk(Clk), .d(RA1), .data(vpe_memory_data_2_data));
  VPE_Memory_Data vpe_memory_data_3 (.Addr(RB2), .WM(V_WM), .Clk(Clk), .d(RA2), .data(vpe_memory_data_3_data));
  VPE_ULA vpe_ula_4 (.ULA_Op(V_UOp), .RA(DE3), .RB(multiplexer_29_out), .out_4(vpe_ula_4_out_4));
  SPE_ULA spe_ula_1 (.ULA_Op(UOp), .RA(DE), .RB(multiplexer_27_out), .out_4(RiUla));
  Multiplexer #(.width(8)) multiplexer_30 (.in0(vpe_ula_1_out_4), .in1(vpe_memory_data_1_data), .out(d0), .sel(V_MD));
  Multiplexer #(.width(8)) multiplexer_31 (.in0(vpe_ula_2_out_4), .in1(vpe_memory_data_2_data), .out(d1), .sel(V_MD));
  Multiplexer #(.width(8)) multiplexer_32 (.in0(vpe_ula_3_out_4), .in1(vpe_memory_data_3_data), .out(d2), .sel(V_MD));
  Multiplexer #(.width(3)) multiplexer_33 (.in0(3'b000), .in1(V_WB), .out(WB_ID), .sel(Vec));
  Adder adder_5 (.a(8'h4), .b(RB3), .out(N_Ptr3));  // open: cin, cout
  VPE_Memory_Data vpe_memory_data_4 (.Addr(AE3), .WM(V_WM), .Clk(Clk), .d(DE3), .data(vpe_memory_data_4_data));
  Multiplexer #(.width(8)) multiplexer_34 (.in0(vpe_ula_4_out_4), .in1(vpe_memory_data_4_data), .out(d3), .sel(V_MD));
  Stg_EX_MEM_Spe stg_ex_mem_spe_1 (
    .AddrR_Exe(RD_EX), .MemSgn_Exe(MS_Ex), .WbSgn_Exe(WS_Ex), .UlaR_Exe(RiUla), .Addr_Exe(AE), .Data_Exe(DE),
    .Clk(Clk), .R(R), .AddrR_Mem(RD_ME), .MemSgn_Mem({W, MD}), .WbSgn_Mem(WS_Me), .UlaR_Mem(RUla),
    .Addr_Mem(Addr), .Data_Mem(d));
  SPE_Memory_Data spe_memory_data_1 (.Addr(Addr), .WM(W), .Clk(Clk), .d(d), .data(spe_memory_data_1_data));
  Multiplexer #(.width(8)) multiplexer_35 (
    .in0(RUla), .in1(spe_memory_data_1_data), .out(multiplexer_35_out), .sel(MD));
  Stg_MEM_WB_Spe stg_mem_wb_spe_1 (
    .AddrR_Mem(RD_ME), .WbSgn_Mem(WS_Me), .Data_Mem(multiplexer_35_out), .Clk(Clk), .R(R), .AddrR_WB(RD_WB),
    .WbSgn_WB(WE), .Data_WB(RWB));

  // Other names for the same wires on the sheet: RD_ID[1:0] = RA_ID; RAD = ID[0]; ID[1] = Br

  // Notes on the sheet:
  //   VPE: control signs
  //   VPE: Register bank's control signs
  //   =============================== Vector Processing Element ===============================
  //   =============================== Scalar Processing Element ===============================
  //   VPE: ALU's control signs
  //   ================== VPE0 ==================
  //   ================== VPE1 ==================
  //   ================== VPE2 ==================
  //   ================== VPE3 ==================
  //   VPE: Memory's control signs
  //   Next address
  //   Next address
  //   Next address
  //   VPE: Write back's control signs
  //   Next address
endmodule

module Program_Counter (
  input  [7:0] PC_P,
  input  En,
  input  Clk,
  input  R,
  output [7:0] PC_N
);

  Register PC (.D(PC_P), .en(En), .clk(Clk), .Q(PC_N), .clr(R));
endmodule

module Memory_Instruction (
  input  [7:0] Addr_PC,
  output [7:0] Inst
);

  ROM rom_1 (.addr(Addr_PC), .data(Inst));

  // Notes on the sheet:
  //   contents of rom_1 (hex, n*v repeats v):
  //   c8 cc b4 32 49 ee 3d 79 cd 31 59 35 71 32 49 bc cd b4 ee 21 3d 79 cd 20 31 59 21 32 71 55 32 49 b0
  //   e6 22 3b 79 20 31 59 22 31 71 55 32 49 da c8 8e a0 bc c9 86 cd a0 bc c9 9e 24 36 79 20 31 59 a1 b4
  //   d9 23 30 71 70
endmodule

module Control_Unit (
  input  [3:0] Opcode,
  output Vec,
  output WESpe,
  output RadSpe,
  output [2:0] UlaOpSpe,
  output [1:0] UlaSrSpe,
  output BrSpe,
  output MDSpe,
  output WMSpe,
  output [9:0] VecSg
);

  ROM #(.addrWidth(4), .dataWidth(21)) rom_1 (
    .addr(Opcode), .data({Vec, WESpe, RadSpe, UlaOpSpe, UlaSrSpe, BrSpe, MDSpe, WMSpe, VecSg}));

  // Notes on the sheet:
  //   contents of rom_1 (hex, n*v repeats v):
  //   80800 400 c2000 ca000 90000 98000 a0000 5000 100202 100001 100304 10030c 100210 100218 1002c1 100220
  //   Total de bits: 21
  //   0..9: signs of the vector part
  //   10..20: signs of the scalar part
  //   21: control bit between scalar and vector instructions
endmodule

module SPE_Register_Bank (
  input  [7:0] Data,
  input  [1:0] RA,
  input  WE,
  input  [1:0] RD,
  input  [1:0] RB,
  input  Clk,
  input  R,
  output [7:0] RD1,
  output [7:0] RD2
);

  wire demultiplexer_1_out0, R1, R2, R3;
  wire [7:0] D1, D2, D3;

  // NoConnect on demultiplexer_1_out0
  Demultiplexer #(.select(2)) demultiplexer_1 (
    .out0(demultiplexer_1_out0), .out1(R1), .out2(R2), .out3(R3), .in(WE), .sel(RD));
  Register #(.trigger("falling")) SR1 (.D(Data), .en(R1), .clk(Clk), .Q(D1), .clr(R));
  Register #(.trigger("falling")) SR2 (.D(Data), .en(R2), .clk(Clk), .Q(D2), .clr(R));
  Register #(.trigger("falling")) SR3 (.D(Data), .en(R3), .clk(Clk), .Q(D3), .clr(R));
  Multiplexer #(.select(2), .width(8)) multiplexer_1 (
    .in0({8{1'b0}}), .in1(D1), .in2(D2), .in3(D3), .out(RD1), .sel(RA));
  Multiplexer #(.select(2), .width(8)) multiplexer_2 (
    .in0({8{1'b0}}), .in1(D1), .in2(D2), .in3(D3), .out(RD2), .sel(RB));

  // Notes on the sheet:
  //   SR0
endmodule

module SPE_ULA (
  input  [7:0] RA,
  input  [7:0] RB,
  input  [2:0] ULA_Op,
  output [7:0] out_4
);

  wire [7:0] R2, R3, R4;

  // NoConnect on RA[7:4]
  // NoConnect on RB[7:4]
  // NoConnect on RB[7:4]
  // NoConnect on RA[3:0]
  Adder adder_1 (.a(RA), .b(RB), .out(R2));  // open: cin, cout
  Subtractor subtractor_1 (.a(RA), .b(RB), .out(R3));  // open: bin, bout
  assign R4 = RA & RB;  // AND_Gate and_1, 8 bits wide
  Multiplexer #(.select(3), .width(8)) multiplexer_1 (
    .in0({RB[3:0], RA[3:0]}), .in1({RA[7:4], RB[3:0]}), .in2(R2), .in3(R3), .in4(R4), .in5({8{1'b0}}),
    .in6({8{1'b0}}), .in7({8{1'b0}}), .out(out_4), .sel(ULA_Op));

  // Other names for the same wires on the sheet: R0[7:0] = {RB[3:0], RA[3:0]}; R1[7:0] = {RA[7:4], RB[3:0]}

  // Notes on the sheet:
  //   Move High
  //   Move Low
  //   Adder
  //   Subtractor
  //   AND
endmodule

module SPE_Memory_Data (
  input  [7:0] Addr,
  input  WM,
  input  Clk,
  input  [7:0] d,
  output [7:0] data
);

  RAM ram_1 (.addr(Addr), .we(WM), .oe(1'b1), .clk(Clk), .din(d), .dout(data));
endmodule

module VPE_Ctrl (
  input  [9:0] VectorSigns,
  output ID_V,
  output [3:0] EXE_V,
  output [1:0] MEM_V,
  output [2:0] WB_V
);


  assign EXE_V = {VectorSigns[2], VectorSigns[5:3]};
  assign ID_V = VectorSigns[8];
  assign MEM_V = VectorSigns[1:0];
  assign WB_V = {VectorSigns[9], VectorSigns[7:6]};
endmodule

module VPE0_Register_Bank (
  input  [7:0] Data,
  input  [1:0] RA,
  input  WE,
  input  [1:0] RD,
  input  [1:0] RB,
  input  Clk,
  input  R,
  output [7:0] RD1,
  output [7:0] RD2
);

  wire demultiplexer_1_out0, R1, R2, R3;
  wire [7:0] D1, D2, D3;

  // NoConnect on demultiplexer_1_out0
  Demultiplexer #(.select(2)) demultiplexer_1 (
    .out0(demultiplexer_1_out0), .out1(R1), .out2(R2), .out3(R3), .in(WE), .sel(RD));
  Register VR1 (.D(Data), .en(R1), .clk(Clk), .Q(D1), .clr(R));
  Register VR2 (.D(Data), .en(R2), .clk(Clk), .Q(D2), .clr(R));
  Register VR3 (.D(Data), .en(R3), .clk(Clk), .Q(D3), .clr(R));
  Multiplexer #(.select(2), .width(8)) multiplexer_1 (
    .in0({8{1'b0}}), .in1(D1), .in2(D2), .in3(D3), .out(RD1), .sel(RA));
  Multiplexer #(.select(2), .width(8)) multiplexer_2 (
    .in0({8{1'b0}}), .in1(D1), .in2(D2), .in3(D3), .out(RD2), .sel(RB));

  // Notes on the sheet:
  //   VR0
endmodule

module VPE1_Register_Bank (
  input  [7:0] Data,
  input  [1:0] RA,
  input  WE,
  input  [1:0] RD,
  input  [1:0] RB,
  input  Clk,
  input  R,
  output [7:0] RD1,
  output [7:0] RD2
);

  wire demultiplexer_1_out0, R1, R2, R3;
  wire [7:0] D1, D2, D3;

  // NoConnect on demultiplexer_1_out0
  Demultiplexer #(.select(2)) demultiplexer_1 (
    .out0(demultiplexer_1_out0), .out1(R1), .out2(R2), .out3(R3), .in(WE), .sel(RD));
  Register VR1 (.D(Data), .en(R1), .clk(Clk), .Q(D1), .clr(R));
  Register VR2 (.D(Data), .en(R2), .clk(Clk), .Q(D2), .clr(R));
  Register VR3 (.D(Data), .en(R3), .clk(Clk), .Q(D3), .clr(R));
  Multiplexer #(.select(2), .width(8)) multiplexer_1 (.in0(8'h1), .in1(D1), .in2(D2), .in3(D3), .out(RD1), .sel(RA));
  Multiplexer #(.select(2), .width(8)) multiplexer_2 (.in0(8'h1), .in1(D1), .in2(D2), .in3(D3), .out(RD2), .sel(RB));

  // Notes on the sheet:
  //   VR0
endmodule

module VPE2_Register_Bank (
  input  [7:0] Data,
  input  [1:0] RA,
  input  WE,
  input  [1:0] RD,
  input  [1:0] RB,
  input  Clk,
  input  R,
  output [7:0] RD1,
  output [7:0] RD2
);

  wire demultiplexer_1_out0, R1, R2, R3;
  wire [7:0] D1, D2, D3;

  // NoConnect on demultiplexer_1_out0
  Demultiplexer #(.select(2)) demultiplexer_1 (
    .out0(demultiplexer_1_out0), .out1(R1), .out2(R2), .out3(R3), .in(WE), .sel(RD));
  Register VR1 (.D(Data), .en(R1), .clk(Clk), .Q(D1), .clr(R));
  Register VR2 (.D(Data), .en(R2), .clk(Clk), .Q(D2), .clr(R));
  Register VR3 (.D(Data), .en(R3), .clk(Clk), .Q(D3), .clr(R));
  Multiplexer #(.select(2), .width(8)) multiplexer_1 (.in0(8'h2), .in1(D1), .in2(D2), .in3(D3), .out(RD1), .sel(RA));
  Multiplexer #(.select(2), .width(8)) multiplexer_2 (.in0(8'h2), .in1(D1), .in2(D2), .in3(D3), .out(RD2), .sel(RB));

  // Notes on the sheet:
  //   VR0
endmodule

module VPE3_Register_Bank (
  input  [7:0] Data,
  input  [1:0] RA,
  input  WE,
  input  [1:0] RD,
  input  [1:0] RB,
  input  Clk,
  input  R,
  output [7:0] RD1,
  output [7:0] RD2
);

  wire demultiplexer_1_out0, R1, R2, R3;
  wire [7:0] D1, D2, D3;

  // NoConnect on demultiplexer_1_out0
  Demultiplexer #(.select(2)) demultiplexer_1 (
    .out0(demultiplexer_1_out0), .out1(R1), .out2(R2), .out3(R3), .in(WE), .sel(RD));
  Register VR1 (.D(Data), .en(R1), .clk(Clk), .Q(D1), .clr(R));
  Register VR2 (.D(Data), .en(R2), .clk(Clk), .Q(D2), .clr(R));
  Register VR3 (.D(Data), .en(R3), .clk(Clk), .Q(D3), .clr(R));
  Multiplexer #(.select(2), .width(8)) multiplexer_1 (.in0(8'h3), .in1(D1), .in2(D2), .in3(D3), .out(RD1), .sel(RA));
  Multiplexer #(.select(2), .width(8)) multiplexer_2 (.in0(8'h3), .in1(D1), .in2(D2), .in3(D3), .out(RD2), .sel(RB));

  // Notes on the sheet:
  //   VR0
endmodule

module VPE_ULA (
  input  [7:0] RA,
  input  [7:0] RB,
  input  [2:0] ULA_Op,
  output [7:0] out_4
);

  wire comparator_1_eq;
  wire [7:0] R2, R3, R4;

  // NoConnect on RA[7:4]
  // NoConnect on RB[7:4]
  // NoConnect on RB[7:4]
  // NoConnect on RA[3:0]
  Adder adder_1 (.a(RA), .b(RB), .out(R2));  // open: cin, cout
  Subtractor subtractor_1 (.a(RA), .b(RB), .out(R3));  // open: bin, bout
  assign R4 = {{7{comparator_1_eq}}, comparator_1_eq};  // Bit_Extender bit_extender_1
  Comparator comparator_1 (.a(RA), .b(RB), .eq(comparator_1_eq));  // open: gt, lt
  Multiplexer #(.select(3), .width(8)) multiplexer_1 (
    .in0({RB[3:0], RA[3:0]}), .in1({RA[7:4], RB[3:0]}), .in2(R2), .in3(R3), .in4(R4), .in5({8{1'b0}}),
    .in6({8{1'b0}}), .in7({8{1'b0}}), .out(out_4), .sel(ULA_Op));

  // Other names for the same wires on the sheet: R0[7:0] = {RB[3:0], RA[3:0]}; R1[7:0] = {RA[7:4], RB[3:0]}

  // Notes on the sheet:
  //   Move High
  //   Move Low
  //   Adder
  //   Subtractor
  //   Comparator
endmodule

module VPE_Memory_Data (
  input  [7:0] Addr,
  input  WM,
  input  Clk,
  input  [7:0] d,
  output [7:0] data
);

  RAM #(.trigger("falling")) ram_1 (.addr(Addr), .we(WM), .oe(1'b1), .clk(Clk), .din(d), .dout(data));
endmodule

module Stg_IF_ID (
  input  [7:0] Inst_IF,
  input  En,
  input  Clk,
  input  R,
  output [7:0] Inst_ID
);

  Register Inst (.D(Inst_IF), .en(En), .clk(Clk), .Q(Inst_ID), .clr(R));
endmodule

module Stg_ID_EX_Spe (
  input  [4:0] ExeSgn_Id,
  input  [1:0] MemSgn_Id,
  input  WbSgn_Id,
  input  [7:0] RD1_Id,
  input  [7:0] RD2_Id,
  input  [5:0] ARs_Id,
  input  [7:0] Imm_Id,
  input  Clk,
  input  R,
  output [4:0] ExeSgn_Exe,
  output [1:0] MemSgn_Exe,
  output WbSgn_Exe,
  output [7:0] RD1_Exe,
  output [7:0] RD2_Exe,
  output [5:0] ARs_Exe,
  output [7:0] Imm_Exe
);

  wire undriven;

  Register #(.width(5)) EXE (.D(ExeSgn_Id), .en(1'b1), .clk(Clk), .Q(ExeSgn_Exe), .clr(undriven));
  Register #(.width(2)) MEM (.D(MemSgn_Id), .en(1'b1), .clk(Clk), .Q(MemSgn_Exe), .clr(undriven));
  Register #(.width(1)) WB (.D(WbSgn_Id), .en(1'b1), .clk(Clk), .Q(WbSgn_Exe), .clr(undriven));
  Register RD1 (.D(RD1_Id), .en(1'b1), .clk(Clk), .Q(RD1_Exe), .clr(undriven));
  Register RD2 (.D(RD2_Id), .en(1'b1), .clk(Clk), .Q(RD2_Exe), .clr(undriven));
  Register #(.width(6)) AdRs (.D(ARs_Id), .en(1'b1), .clk(Clk), .Q(ARs_Exe), .clr(undriven));
  Register Imm (.D(Imm_Id), .en(1'b1), .clk(Clk), .Q(Imm_Exe), .clr(R));
endmodule

module Stg_ID_EX_Vpe (
  input  [3:0] ExeSgn_Id,
  input  [1:0] MemSgn_Id,
  input  [2:0] WbSgn_Id,
  input  [7:0] RD1_Id,
  input  [7:0] RD2_Id,
  input  [5:0] ARs_Id,
  input  [7:0] Imm_Id,
  input  Clk,
  input  R,
  output [3:0] ExeSgn_Exe,
  output [1:0] MemSgn_Exe,
  output [2:0] WbSgn_Exe,
  output [7:0] RD1_Exe,
  output [7:0] RD2_Exe,
  output [5:0] ARs_Exe,
  output [7:0] Imm_Exe
);

  wire undriven;

  Register #(.width(4)) EXE (.D(ExeSgn_Id), .en(1'b1), .clk(Clk), .Q(ExeSgn_Exe), .clr(undriven));
  Register #(.width(2)) MEM (.D(MemSgn_Id), .en(1'b1), .clk(Clk), .Q(MemSgn_Exe), .clr(undriven));
  Register #(.width(3)) WB (.D(WbSgn_Id), .en(1'b1), .clk(Clk), .Q(WbSgn_Exe), .clr(undriven));
  Register RD1 (.D(RD1_Id), .en(1'b1), .clk(Clk), .Q(RD1_Exe), .clr(undriven));
  Register RD2 (.D(RD2_Id), .en(1'b1), .clk(Clk), .Q(RD2_Exe), .clr(undriven));
  Register #(.width(6)) AdRs (.D(ARs_Id), .en(1'b1), .clk(Clk), .Q(ARs_Exe), .clr(undriven));
  Register Imm (.D(Imm_Id), .en(1'b1), .clk(Clk), .Q(Imm_Exe), .clr(R));
endmodule

module Stg_EX_MEM_Spe (
  input  [1:0] MemSgn_Exe,
  input  WbSgn_Exe,
  input  [7:0] UlaR_Exe,
  input  [7:0] Addr_Exe,
  input  [7:0] Data_Exe,
  input  [1:0] AddrR_Exe,
  input  Clk,
  input  R,
  output [1:0] MemSgn_Mem,
  output WbSgn_Mem,
  output [7:0] UlaR_Mem,
  output [7:0] Addr_Mem,
  output [7:0] Data_Mem,
  output [1:0] AddrR_Mem
);

  wire undriven;

  Register #(.width(2)) MEM (.D(MemSgn_Exe), .en(1'b1), .clk(Clk), .Q(MemSgn_Mem), .clr(undriven));
  Register #(.width(1)) WB (.D(WbSgn_Exe), .en(1'b1), .clk(Clk), .Q(WbSgn_Mem), .clr(undriven));
  Register UlaR (.D(UlaR_Exe), .en(1'b1), .clk(Clk), .Q(UlaR_Mem), .clr(undriven));
  Register Addr (.D(Addr_Exe), .en(1'b1), .clk(Clk), .Q(Addr_Mem), .clr(undriven));
  Register Data (.D(Data_Exe), .en(1'b1), .clk(Clk), .Q(Data_Mem), .clr(undriven));
  Register #(.width(2)) AddrR (.D(AddrR_Exe), .en(1'b1), .clk(Clk), .Q(AddrR_Mem), .clr(R));
endmodule

module Stg_EX_MEM_Vpe (
  input  [2:0] MemSgn_Exe,
  input  [1:0] WbSgn_Exe,
  input  [7:0] UlaR_Exe,
  input  [7:0] Addr_Exe,
  input  [7:0] Data_Exe,
  input  [1:0] AddrR_Exe,
  input  Clk,
  input  R,
  output [2:0] MemSgn_Mem,
  output [1:0] WbSgn_Mem,
  output [7:0] UlaR_Mem,
  output [7:0] Addr_Mem,
  output [7:0] Data_Mem,
  output [1:0] AddrR_Mem
);

  wire undriven;

  Register #(.width(3)) MEM (.D(MemSgn_Exe), .en(1'b1), .clk(Clk), .Q(MemSgn_Mem), .clr(undriven));
  Register #(.width(2)) WB (.D(WbSgn_Exe), .en(1'b1), .clk(Clk), .Q(WbSgn_Mem), .clr(undriven));
  Register UlaR (.D(UlaR_Exe), .en(1'b1), .clk(Clk), .Q(UlaR_Mem), .clr(undriven));
  Register Addr (.D(Addr_Exe), .en(1'b1), .clk(Clk), .Q(Addr_Mem), .clr(undriven));
  Register Data (.D(Data_Exe), .en(1'b1), .clk(Clk), .Q(Data_Mem), .clr(undriven));
  Register #(.width(2)) AddrR (.D(AddrR_Exe), .en(1'b1), .clk(Clk), .Q(AddrR_Mem), .clr(R));
endmodule

module Stg_MEM_WB_Spe (
  input  WbSgn_Mem,
  input  [7:0] Data_Mem,
  input  [1:0] AddrR_Mem,
  input  Clk,
  input  R,
  output WbSgn_WB,
  output [7:0] Data_WB,
  output [1:0] AddrR_WB
);

  wire undriven;

  Register #(.width(1)) WB (.D(WbSgn_Mem), .en(1'b1), .clk(Clk), .Q(WbSgn_WB), .clr(undriven));
  Register Data (.D(Data_Mem), .en(1'b1), .clk(Clk), .Q(Data_WB), .clr(undriven));
  Register #(.width(2)) AddrR (.D(AddrR_Mem), .en(1'b1), .clk(Clk), .Q(AddrR_WB), .clr(R));
endmodule

module Stg_MEM_WB_Vpe (
  input  [1:0] WbSgn_Mem,
  input  [7:0] Data_Mem,
  input  [1:0] AddrR_Mem,
  input  Clk,
  input  R,
  output [1:0] WbSgn_WB,
  output [7:0] Data_WB,
  output [1:0] AddrR_WB
);

  wire undriven;

  Register #(.width(2)) WB (.D(WbSgn_Mem), .en(1'b1), .clk(Clk), .Q(WbSgn_WB), .clr(undriven));
  Register Data (.D(Data_Mem), .en(1'b1), .clk(Clk), .Q(Data_WB), .clr(undriven));
  Register #(.width(2)) AddrR (.D(AddrR_Mem), .en(1'b1), .clk(Clk), .Q(AddrR_WB), .clr(R));
endmodule

module ForwardingULA_Unit (
  input  WE_ExMem,
  input  WE_MemWb,
  input  [1:0] Rd_MemWb,
  input  [1:0] Rd_ExMem,
  input  [1:0] Rb,
  input  [1:0] Ra,
  output [1:0] Forw_A,
  output [1:0] Forw_B
);

  wire comparator_1_eq, comparator_2_eq, comparator_3_eq, comparator_4_eq, comparator_5_eq, comparator_6_eq;
  wire [0:0] and_2_out, and_4_out;
  wire [1:1] and_1_out, and_3_out;

  Comparator #(.mode("unsigned"), .width(2)) comparator_1 (.a(Ra), .b(Rd_ExMem), .eq(comparator_1_eq));  // open: gt, lt
  Comparator #(.mode("unsigned"), .width(2)) comparator_2 (.a(Ra), .b(Rd_MemWb), .eq(comparator_2_eq));  // open: gt, lt
  Comparator #(.mode("unsigned"), .width(2)) comparator_3 (.a(Rb), .b(Rd_ExMem), .eq(comparator_3_eq));  // open: gt, lt
  Comparator #(.mode("unsigned"), .width(2)) comparator_4 (.a(Rb), .b(Rd_MemWb), .eq(comparator_4_eq));  // open: gt, lt
  and and_1 (and_1_out[1], comparator_1_eq, WE_ExMem);
  and and_2 (and_2_out[0], comparator_2_eq, WE_MemWb);
  and and_3 (and_3_out[1], comparator_3_eq, WE_ExMem);
  and and_4 (and_4_out[0], comparator_4_eq, WE_MemWb);
  Comparator #(.mode("unsigned"), .width(2)) comparator_5 (
    .a({and_1_out[1], 1'b0}), .b(2'b00), .eq(comparator_5_eq));  // open: gt, lt
  Comparator #(.mode("unsigned"), .width(2)) comparator_6 (
    .a({and_3_out[1], 1'b0}), .b(2'b00), .eq(comparator_6_eq));  // open: gt, lt
  Multiplexer #(.width(2)) multiplexer_1 (
    .in0({and_1_out[1], 1'b0}), .in1({1'b0, and_2_out[0]}), .out(Forw_A), .sel(comparator_5_eq));
  Multiplexer #(.width(2)) multiplexer_2 (
    .in0({and_3_out[1], 1'b0}), .in1({1'b0, and_4_out[0]}), .out(Forw_B), .sel(comparator_6_eq));
endmodule

module ForwardingBranch_Unit (
  input  WE_IdEx,
  input  WE_ExMem,
  input  [1:0] Rd_ExMem,
  input  [1:0] Rd_IdEx,
  input  [1:0] Ra_id,
  output [1:0] Forw_Br
);

  wire comparator_1_eq, comparator_2_eq, comparator_3_eq;
  wire [0:0] and_2_out;
  wire [1:1] and_1_out;

  Comparator #(.mode("unsigned"), .width(2)) comparator_1 (
    .a(Ra_id), .b(Rd_IdEx), .eq(comparator_1_eq));  // open: gt, lt
  Comparator #(.mode("unsigned"), .width(2)) comparator_2 (
    .a(Ra_id), .b(Rd_ExMem), .eq(comparator_2_eq));  // open: gt, lt
  and and_1 (and_1_out[1], comparator_1_eq, WE_IdEx);
  and and_2 (and_2_out[0], comparator_2_eq, WE_ExMem);
  Comparator #(.mode("unsigned"), .width(2)) comparator_3 (
    .a({and_1_out[1], 1'b0}), .b(2'b00), .eq(comparator_3_eq));  // open: gt, lt
  Multiplexer #(.width(2)) multiplexer_1 (
    .in0({and_1_out[1], 1'b0}), .in1({1'b0, and_2_out[0]}), .out(Forw_Br), .sel(comparator_3_eq));
endmodule

module Hazard_Unit (
  input  [1:0] RD_ex,
  input  [1:0] RB_id,
  input  [1:0] RA_id,
  input  MemRead,
  input  Br,
  output hnop,
  output EN
);

  wire and_1_out, comparator_1_eq, comparator_2_eq, or_1_out;

  Comparator #(.mode("unsigned"), .width(2)) comparator_1 (.a(RA_id), .b(RD_ex), .eq(comparator_1_eq));  // open: gt, lt
  Comparator #(.mode("unsigned"), .width(2)) comparator_2 (.a(RB_id), .b(RD_ex), .eq(comparator_2_eq));  // open: gt, lt
  or or_1 (or_1_out, comparator_1_eq, comparator_2_eq);
  and and_1 (and_1_out, or_1_out, MemRead);
  not not_1 (EN, and_1_out);
  or or_2 (hnop, and_1_out, Br);
endmodule
